# Fritzing sketch Arduino With Load Cell (saved by Fritzing 0.9.3b)
breadboards: 2

parts:
  Part1 = Arduino Uno (Rev3)
  M1 = DC Motor
  IC1 = L293D [package=THT]
  Load_Cell1 = Load Cell - Red/white/black/green
  Part4 = HX711 Weighing Sensor Module
  Part5 = LCD1602-I2C
  VCC1 = 4 x AAA Battery Mount

nets:
  N1: Part1.A4/SDA, Part5.SDA
  N2: Part1.A5/SCL, Part5.SCL
  N3: Part1.D3_PWM, IC1.In_2
  N4: Part1.D4, IC1.In_1
  N5: Part1.D5_PWM, IC1.Enable_1
  N6: Part1.D6_PWM, Part4.DO/RX
  N7: Part1.D7, Part4.CK/TX
  VCC: Part1.5V, Part4.VCC, Part5.VCC
  GND: Part1.GND, Part4.GND, Part5.GND
  N8: M1.pin_1, IC1.Out_2_(_Controlled_by_Enable_1_)
  N9: M1.pin_2, IC1.Out_1_(_Controlled_by_Enable_1_)
  N10: IC1.0V, VCC1.-
  N11: IC1.+Vmotor, VCC1.+
  N12: Load_Cell1.wire1, Part4.E+
  N13: Load_Cell1.wire2, Part4.A+
  N14: Load_Cell1.wire3, Part4.E-
  N15: Load_Cell1.wire4, Part4.A-

custom parts:
  Load Cell - Red/white/black/green: A rectangle load cell/weighting pressure Sensor with four wires - Red, white, black, green. Normally corresponding with E+, E-, A+, A- respectively.
  LCD1602-I2C: A standard character display, usually with 2x16 characters. Comes in many colors with LCM1602 IIC attached.
